# Fritzing sketch accel_four_schematic (saved by Fritzing 0.9.3b)
breadboards: 1

parts:
  Part1 = Arduino Uno (Rev3)
  Q1 = PNP-Transistor [package="TO92 [THT]"]
  Q2 = PNP-Transistor [package="TO92 [THT]"]
  Q3 = PNP-Transistor [package="TO92 [THT]"]
  Q4 = PNP-Transistor [package="TO92 [THT]"]
  R1 = Resistor [tolerance=±5% resistance=100 package=THT]
  R3 = Resistor [tolerance=±5% resistance=100 package=THT]
  R4 = Resistor [tolerance=±5% resistance=100 package=THT]
  Part2 = Triple Axis Magnetometer - HMC5883 Breakout
  Part3 = Triple Axis Magnetometer - HMC5883 Breakout
  Part4 = Triple Axis Magnetometer - HMC5883 Breakout
  R2 = Resistor [tolerance=±5% resistance=100 package=THT]
  Part5 = Triple Axis Magnetometer - HMC5883 Breakout

nets:
  N1: Part1.A4/SDA, Q1.E, Q2.E, Q3.E, Q4.E
  N2: Part1.A5/SCL, Part2.SCL, Part3.SCL, Part4.SCL, Part5.SCL
  N3: Part1.D8, R1.Pin_1
  N4: Part1.D9_PWM, R2.Pin_1
  N5: Part1.D10_PWM/SS, R3.Pin_1
  N6: Part1.D7, R4.Pin_1
  VCC: Part1.5V, Part2.VCC, Part3.VCC, Part4.VCC, Part5.VCC
  GND: Part1.GND, Part2.GND, Part3.GND, Part4.GND, Part5.GND
  N7: Q1.B, R3.Pin_0
  N8: Q1.C, Part3.SDA
  N9: Q2.B, R1.Pin_0
  N10: Q2.C, Part4.SDA
  N11: Q3.B, R4.Pin_0
  N12: Q3.C, Part5.SDA
  N13: Q4.B, R2.Pin_0
  N14: Q4.C, Part2.SDA

notes:
  TIP120 transistors
